# Fritzing sketch Untitled Sketch (saved by Fritzing 0.9.3b)

parts:
  Part1 = Arduino Uno (Rev3)  # not connected
  VCC1 = Battery  # not connected
  M1 = DC Motor
  M2 = DC Motor
  M3 = L293D Motor Driver

nets:
  N1: M1.pin_1, M3.pin_11
  N2: M1.pin_2, M3.pin_12
  N3: M2.pin_1, M3.pin_10
  N4: M2.pin_2, M3.pin_9
