# Fritzing sketch obstacle avoiding (saved by Fritzing 0.9.3b)

parts:
  HC-SR04_Sensor_1 = HC-SR04 Ultrasonic Distance Sensor
  HC-SR04_Sensor_2 = HC-SR04 Ultrasonic Distance Sensor
  HC-SR04_Sensor_3 = HC-SR04 Ultrasonic Distance Sensor
  BAT1 = BC9VPC [package=bc9vpc]  # not connected
  M3 = L293D Motor Driver
  M4 = DC Motor
  M5 = DC Motor
  Part1 = Arduino Mega 2560 (Rev3)

nets:
  VCC: HC-SR04_Sensor_1.VCC, HC-SR04_Sensor_2.VCC, HC-SR04_Sensor_3.VCC, M3.pin_3, Part1.5V
  N1: HC-SR04_Sensor_1.TRIG, Part1.D52
  N2: HC-SR04_Sensor_1.ECHO, Part1.D50
  GND: HC-SR04_Sensor_1.GND, HC-SR04_Sensor_2.GND, HC-SR04_Sensor_3.GND, M3.pin_4, Part1.GND
  N3: HC-SR04_Sensor_2.TRIG, Part1.D44
  N4: HC-SR04_Sensor_2.ECHO, Part1.D42
  N5: HC-SR04_Sensor_3.TRIG, Part1.D48
  N6: HC-SR04_Sensor_3.ECHO, Part1.D46
  N7: M3.pin_5, Part1.D32
  N8: M3.pin_6, Part1.D30
  N9: M3.pin_7, Part1.D24
  N10: M3.pin_8, Part1.D22
  N11: M3.pin_9, M5.pin_1
  N12: M3.pin_10, M5.pin_2
  N13: M3.pin_11, M4.pin_1
  N14: M3.pin_12, M4.pin_2
